// Logisim project procesor.circ as structural Verilog
module MAIN (
);

  wire button_1_out, clock_1_out, prog_1_clk_out;
  wire [3:0] memory_managment_1_op;
  wire [7:0] keyboard_1_data;
  wire [15:0] memory_managment_1_out_a, memory_managment_1_out_b, prog_1_data, prog_1_inst, prog_1_ip,
       ram_1_data, register_1_q, undriven, undriven_2, undriven_3;
  wire [16:0] alu_1_out, memory_managment_1_out_12, memory_managment_1_out_13, memory_managment_1_out_14,
       memory_managment_1_out_15, memory_managment_1_out_16, memory_managment_1_out_17,
       memory_managment_1_out_19;

  Clock clock_1 (.out(clock_1_out));
  Button button_1 (.out(button_1_out));
  // Probe on memory_managment_1_op
  // Probe on memory_managment_1_out_a
  RAM #(.addrWidth(16), .dataWidth(16), .bus("separate")) ram_1 (
    .addr(register_1_q), .din(memory_managment_1_out_13[15:0]), .data(ram_1_data),
    .str(memory_managment_1_out_13[16]), .clk(memory_managment_1_out_13[16]), .clr(button_1_out));  // open: sel, ld
  // Probe on register_1_q
  Register #(.width(16)) register_1 (
    .D(memory_managment_1_out_12[15:0]), .Q(register_1_q), .clk(memory_managment_1_out_12[16]),
    .clr(button_1_out));  // open: en
  // Probe on prog_1_ip
  // Probe on prog_1_inst
  // Probe on prog_1_data
  PROG prog_1 (
    .IP_WRT(memory_managment_1_out_19), .CLK_IN(clock_1_out), .IP(prog_1_ip), .CLK_OUT(prog_1_clk_out),
    .INST(prog_1_inst), .DATA(prog_1_data), .RESET(button_1_out));
  MEMORY_MANAGMENT memory_managment_1 (
    .IN_0(register_1_q), .IN_0_2(ram_1_data), .IN_0_3({{8{1'b0}}, keyboard_1_data}), .IN_0_4(undriven),
    .IN_0_5(undriven_2), .IN_0_6(undriven_3), .IN_0_7(prog_1_ip), .IN_0_8(prog_1_data),
    .out_12(memory_managment_1_out_12), .out_13(memory_managment_1_out_13),
    .out_14(memory_managment_1_out_14), .out_15(memory_managment_1_out_15),
    .out_16(memory_managment_1_out_16), .out_17(memory_managment_1_out_17),
    .out_19(memory_managment_1_out_19), .INSTR(prog_1_inst), .CLK(prog_1_clk_out),
    .OP(memory_managment_1_op), .OUT_A(memory_managment_1_out_a), .OUT_B(memory_managment_1_out_b),
    .IN(alu_1_out));  // open: out_20
  // Probe on memory_managment_1_out_b
  ALU alu_1 (.OP(memory_managment_1_op), .A(memory_managment_1_out_a), .B(memory_managment_1_out_b), .OUT(alu_1_out));
  Keyboard keyboard_1 (
    .clk(memory_managment_1_out_14[16]), .clr(button_1_out), .avail(keyboard_1_data[7]),
    .data(keyboard_1_data[6:0]));  // open: re
  TTY tty_1 (
    .data(memory_managment_1_out_15[6:0]), .clk(memory_managment_1_out_15[16]), .clr(button_1_out));  // open: we
endmodule

module TEST_ADDER (
  input  in_1,
  input  in_2,
  input  in_3,
  input  in_4,
  input  in_5,
  input  in_6,
  input  in_7,
  input  in_8,
  input  in_9,
  input  in_10,
  input  in_11,
  input  in_12,
  input  in_13,
  input  in_14,
  input  in_15,
  input  in_16,
  input  in_17,
  input  in_18,
  output out_19,
  output out_20,
  output out_21,
  output out_22,
  output out_23,
  output out_24,
  output out_25,
  output out_26
);

  wire adder_1_cout, adder_2_cout, adder_3_cout, adder_4_cout, adder_5_cout, adder_6_cout, adder_7_cout,
       adder_8_cout, xor_1_out, xor_2_out, xor_3_out, xor_4_out, xor_5_out, xor_6_out, xor_7_out, xor_8_out,
       xor_9_out;

  xor xor_1 (xor_1_out, in_2, in_3);
  xor xor_2 (xor_2_out, in_2, in_5);
  xor xor_3 (xor_3_out, in_2, in_7);
  xor xor_4 (xor_4_out, in_2, in_9);
  xor xor_5 (xor_5_out, in_2, in_11);
  xor xor_6 (xor_6_out, in_2, in_13);
  xor xor_7 (xor_7_out, in_2, in_15);
  xor xor_8 (xor_8_out, in_2, in_17);
  xor xor_9 (xor_9_out, in_2, in_1);
  Adder #(.width(1)) adder_1 (.a(xor_1_out), .b(in_4), .out(out_19), .cin(xor_9_out), .cout(adder_1_cout));
  Adder #(.width(1)) adder_2 (.a(xor_2_out), .b(in_6), .out(out_20), .cin(adder_1_cout), .cout(adder_2_cout));
  Adder #(.width(1)) adder_3 (.a(xor_3_out), .b(in_8), .out(out_21), .cin(adder_2_cout), .cout(adder_3_cout));
  Adder #(.width(1)) adder_4 (.a(xor_4_out), .b(in_10), .out(out_22), .cin(adder_3_cout), .cout(adder_4_cout));
  Adder #(.width(1)) adder_5 (.a(xor_5_out), .b(in_12), .out(out_23), .cin(adder_4_cout), .cout(adder_5_cout));
  Adder #(.width(1)) adder_6 (.a(xor_6_out), .b(in_14), .out(out_24), .cin(adder_5_cout), .cout(adder_6_cout));
  Adder #(.width(1)) adder_7 (.a(xor_7_out), .b(in_16), .out(out_25), .cin(adder_6_cout), .cout(adder_7_cout));
  Adder #(.width(1)) adder_8 (.a(xor_8_out), .b(in_18), .out(out_26), .cin(adder_7_cout), .cout(adder_8_cout));
  // XOR_Gate xor_10 has open pins: in0=in_2, in1=adder_8_cout, out=open
endmodule

module ALU (
  input  [3:0] OP,
  input  [15:0] A,
  input  [15:0] B,
  output [16:0] OUT
);

  wire [3:0] bit_extender_2_out, bit_extender_3_out, bit_extender_4_out;
  wire [15:0] adder_1_out, and_1_out, bit_extender_1_out, divider_1_rem, is_not_zero_1_out_2,
       multiplier_1_out, or_1_out, shifter_1_out, shifter_2_out, shifter_3_out, xor_1_out, xor_2_out;
  wire [16:16] not_1_out;

  assign bit_extender_1_out = {{15{OP[0]}}, OP[0]};  // Bit_Extender bit_extender_1
  Bit_Extender #(.in_width(16), .out_width(4)) bit_extender_2 (.in(B), .out(bit_extender_2_out));
  Bit_Extender #(.in_width(16), .out_width(4)) bit_extender_3 (.in(B), .out(bit_extender_3_out));
  Bit_Extender #(.in_width(16), .out_width(4)) bit_extender_4 (.in(B), .out(bit_extender_4_out));
  assign xor_1_out = bit_extender_1_out ^ B;  // XOR_Gate xor_1, 16 bits wide
  IS_NOT_ZERO is_not_zero_1 (.in_1(A), .out_2(is_not_zero_1_out_2));
  Adder #(.width(16)) adder_1 (.a(A), .b(xor_1_out), .out(adder_1_out), .cin(OP[0]));  // open: cout
  Multiplier #(.width(16)) multiplier_1 (.a(A), .b(B), .out(multiplier_1_out));  // open: cin, cout
  Divider #(.width(16)) divider_1 (.a(A), .b(B), .rem(divider_1_rem));  // open: out, upper
  not not_1 (not_1_out[16], A[15]);
  Shifter #(.width(16)) shifter_1 (.in(A), .\dist (bit_extender_2_out), .out(shifter_1_out));
  Shifter #(.width(16), .shift("lr")) shifter_2 (.in(A), .\dist (bit_extender_3_out), .out(shifter_2_out));
  Shifter #(.width(16), .shift("rl")) shifter_3 (.in(A), .\dist (bit_extender_4_out), .out(shifter_3_out));
  assign or_1_out = A | B;  // OR_Gate or_1, 16 bits wide
  assign and_1_out = A & B;  // AND_Gate and_1, 16 bits wide
  assign xor_2_out = A ^ B;  // XOR_Gate xor_2, 16 bits wide
  Multiplexer #(.select(4), .width(17), .enable("false")) multiplexer_1 (
    .in0({1'b1, adder_1_out}), .in1({1'b1, adder_1_out}), .in2({1'b1, multiplier_1_out}),
    .in3({1'b1, divider_1_rem}), .in4({1'b1, is_not_zero_1_out_2}), .in5({not_1_out[16], B}),
    .in6({A[15], B}), .in7({1'b1, A}), .in8({1'b1, shifter_1_out}), .in9({1'b1, shifter_2_out}),
    .in10({1'b1, shifter_3_out}), .in11({1'b1, or_1_out}), .in12({1'b1, and_1_out}),
    .in13({1'b1, xor_2_out}), .out(OUT), .sel(OP));  // open: in14, in15
endmodule

module MEMORY_MANAGMENT (
  input  CLK,
  input  [15:0] INSTR,
  input  [16:0] IN,
  input  [15:0] IN_0,
  input  [15:0] IN_0_2,
  input  [15:0] IN_0_3,
  input  [15:0] IN_0_4,
  input  [15:0] IN_0_5,
  input  [15:0] IN_0_6,
  input  [15:0] IN_0_7,
  input  [15:0] IN_0_8,
  output [16:0] out_12,
  output [16:0] out_13,
  output [16:0] out_14,
  output [16:0] out_15,
  output [16:0] out_16,
  output [16:0] out_17,
  output [3:0] OP,
  output [16:0] out_19,
  output [16:0] out_20,
  output [15:0] OUT_A,
  output [15:0] OUT_B
);

  wire and_2_out, not_1_out;
  wire [15:0] multiplexer_1_out, multiplexer_2_out, registers_1_out_a, registers_1_out_b;
  wire [16:16] and_1_out;

  and and_1 (and_1_out[16], CLK, IN[16]);
  not not_1 (not_1_out, INSTR[11]);
  REGISTERS registers_1 (
    .WRITE_CLK(and_2_out), .A_ID(INSTR[2:0]), .B_ID(INSTR[6:4]), .WRITE_ID(INSTR[10:8]), .IN(IN[15:0]),
    .OUT_A(registers_1_out_a), .OUT_B(registers_1_out_b));
  and and_2 (and_2_out, not_1_out, and_1_out[16]);
  Multiplexer #(.select(3), .width(16)) multiplexer_1 (
    .in0(IN_0), .in1(IN_0_2), .in2(IN_0_3), .in3(IN_0_4), .in4(IN_0_5), .in5(IN_0_6), .in6(IN_0_7),
    .in7(IN_0_8), .out(multiplexer_1_out), .sel(INSTR[2:0]));  // open: en
  Multiplexer #(.select(3), .width(16)) multiplexer_2 (
    .in0(IN_0), .in1(IN_0_2), .in2(IN_0_3), .in3(IN_0_4), .in4(IN_0_5), .in5(IN_0_6), .in6(IN_0_7),
    .in7(IN_0_8), .out(multiplexer_2_out), .sel(INSTR[6:4]));  // open: en
  Demultiplexer #(.select(3), .width(17), .disabled(0)) demultiplexer_1 (
    .out0(out_12), .out1(out_13), .out2(out_14), .out3(out_15), .out4(out_16), .out5(out_17), .out6(out_19),
    .out7(out_20), .in({and_1_out[16], IN[15:0]}), .sel(INSTR[10:8]), .en(INSTR[11]));
  Multiplexer #(.width(16), .enable("false")) multiplexer_3 (
    .in0(registers_1_out_a), .in1(multiplexer_1_out), .out(OUT_A), .sel(INSTR[3]));
  Multiplexer #(.width(16), .enable("false")) multiplexer_4 (
    .in0(registers_1_out_b), .in1(multiplexer_2_out), .out(OUT_B), .sel(INSTR[7]));

  assign OP = INSTR[15:12];
endmodule

module REGISTERS (
  input  [15:0] IN,
  input  WRITE_CLK,
  input  [2:0] A_ID,
  input  [2:0] B_ID,
  input  [2:0] WRITE_ID,
  output [15:0] OUT_A,
  output [15:0] OUT_B
);

  wire demultiplexer_1_out0, demultiplexer_1_out1, demultiplexer_1_out2, demultiplexer_1_out3,
       demultiplexer_1_out4, demultiplexer_1_out5, demultiplexer_1_out6, demultiplexer_1_out7;
  wire [15:0] register_1_q, register_2_q, register_3_q, register_4_q, register_5_q, register_6_q,
       register_7_q, register_8_q;

  Demultiplexer #(.select(3), .disabled(0), .enable("false")) demultiplexer_1 (
    .out0(demultiplexer_1_out0), .out1(demultiplexer_1_out1), .out2(demultiplexer_1_out2),
    .out3(demultiplexer_1_out3), .out4(demultiplexer_1_out4), .out5(demultiplexer_1_out5),
    .out6(demultiplexer_1_out6), .out7(demultiplexer_1_out7), .in(WRITE_CLK), .sel(WRITE_ID));
  Register #(.width(16)) register_1 (.D(IN), .Q(register_1_q), .clk(demultiplexer_1_out0));  // open: en, clr
  Register #(.width(16)) register_2 (.D(IN), .Q(register_2_q), .clk(demultiplexer_1_out1));  // open: en, clr
  Register #(.width(16)) register_3 (.D(IN), .Q(register_3_q), .clk(demultiplexer_1_out2));  // open: en, clr
  Register #(.width(16)) register_4 (.D(IN), .Q(register_4_q), .clk(demultiplexer_1_out3));  // open: en, clr
  Register #(.width(16)) register_5 (.Q(register_5_q), .clk(demultiplexer_1_out4));  // open: D, en, clr
  Register #(.width(16)) register_6 (.D(IN), .Q(register_6_q), .clk(demultiplexer_1_out5));  // open: en, clr
  Register #(.width(16)) register_7 (.D(IN), .Q(register_7_q), .clk(demultiplexer_1_out6));  // open: en, clr
  Register #(.width(16)) register_8 (.D(IN), .Q(register_8_q), .clk(demultiplexer_1_out7));  // open: en, clr
  Multiplexer #(.select(3), .width(16), .disabled(0), .enable("false")) multiplexer_1 (
    .in0(register_1_q), .in1(register_2_q), .in2(register_3_q), .in3(register_4_q), .in4(register_5_q),
    .in5(register_6_q), .in6(register_7_q), .in7(register_8_q), .out(OUT_A), .sel(A_ID));
  Multiplexer #(.select(3), .width(16), .disabled(0), .enable("false")) multiplexer_2 (
    .in0(register_1_q), .in1(register_2_q), .in2(register_3_q), .in3(register_4_q), .in4(register_5_q),
    .in5(register_6_q), .in6(register_7_q), .in7(register_8_q), .out(OUT_B), .sel(B_ID));

  // Notes on the sheet:
  //   OUT
endmodule

module PROG (
  input  CLK_IN,
  input  [16:0] IP_WRT,
  input  RESET,
  output [15:0] IP,
  output [15:0] INST,
  output [15:0] DATA,
  output CLK_OUT
);

  wire and_1_out, and_3_out, and_4_out, not_1_out, not_2_out, not_3_out, not_4_out, or_1_out, or_2_out,
       or_3_out, register_3_q;
  wire [15:0] adder_1_out, multiplexer_1_out;

  Multiplexer #(.width(16), .enable("false")) multiplexer_1 (
    .in0(adder_1_out), .in1(IP_WRT[15:0]), .out(multiplexer_1_out), .sel(IP_WRT[16]));
  Register #(.width(16), .trigger("falling")) register_1 (
    .D(multiplexer_1_out), .Q(IP), .clk(CLK_IN), .clr(RESET));  // open: en
  Adder #(.width(16)) adder_1 (.a(IP), .b(16'h1), .out(adder_1_out));  // open: cin, cout
  and and_1 (and_1_out, CLK_IN, not_1_out);
  not not_1 (not_1_out, RESET);
  ROM #(.addrWidth(16), .dataWidth(16)) rom_1 (.addr(IP), .data(DATA));  // open: sel
  or or_1 (or_1_out, RESET, not_2_out);
  and and_2 (CLK_OUT, and_1_out, or_2_out);
  Register #(.width(16), .trigger("low")) register_2 (.D(DATA), .en(or_1_out), .Q(INST), .clk(and_1_out));  // open: clr
  not not_2 (not_2_out, register_3_q);
  and and_3 (and_3_out, DATA[0], DATA[1], DATA[2], DATA[3]);
  and and_4 (and_4_out, DATA[4], DATA[5], DATA[6], DATA[7]);
  not not_3 (not_3_out, or_2_out);
  or or_2 (or_2_out, register_3_q, not_4_out);
  or or_3 (or_3_out, and_3_out, and_4_out);
  Register #(.width(1), .trigger("falling")) register_3 (
    .D(not_3_out), .Q(register_3_q), .clk(and_1_out), .clr(RESET));  // open: en
  not not_4 (not_4_out, or_3_out);

  // Notes on the sheet:
  //   contents of rom_1 (hex, n*v repeats v):
  //   d000 710f 1 720f a 730f 80 d888 790a 1739 6ef7 8 d939 7a00 7b09 d729 4707 818 6ef7 8 d888 7e0f 15
endmodule

module GPU (
  input  [16:0] RAW_DATA,
  input  [16:0] COMMAND,
  output [15:0] out_3,
  output [15:0] out_4,
  output [15:0] out_5,
  output [15:0] out_6,
  output [15:0] out_7,
  output [15:0] out_8,
  output [15:0] out_9,
  output [15:0] out_10,
  output [15:0] out_11,
  output [15:0] out_12,
  output [15:0] out_13,
  output [15:0] out_14,
  output [15:0] out_15,
  output [15:0] out_16,
  output [15:0] out_17,
  output [15:0] out_18
);

  wire demultiplexer_1_out0, demultiplexer_1_out1, demultiplexer_1_out2, demultiplexer_1_out3,
       demultiplexer_1_out4, demultiplexer_1_out5, demultiplexer_1_out6, demultiplexer_1_out7,
       demultiplexer_1_out8, demultiplexer_1_out9, demultiplexer_1_out10, demultiplexer_1_out11,
       demultiplexer_1_out12, demultiplexer_1_out13, demultiplexer_1_out14, demultiplexer_1_out15,
       demultiplexer_2_out0, demultiplexer_2_out2, demultiplexer_2_out3, undriven_3, undriven_4, undriven_5,
       undriven_6;
  wire [3:0] undriven_2;
  wire [15:0] display_col_1_out_9, undriven;

  Counter #(.width(4), .max('hf)) counter_1 (.clr(demultiplexer_2_out0));  // open: load, D, count, Q, carry, clk
  Demultiplexer #(.select(4)) demultiplexer_1 (
    .out0(demultiplexer_1_out0), .out1(demultiplexer_1_out1), .out2(demultiplexer_1_out2),
    .out3(demultiplexer_1_out3), .out4(demultiplexer_1_out4), .out5(demultiplexer_1_out5),
    .out6(demultiplexer_1_out6), .out7(demultiplexer_1_out7), .out8(demultiplexer_1_out8),
    .out9(demultiplexer_1_out9), .out10(demultiplexer_1_out10), .out11(demultiplexer_1_out11),
    .out12(demultiplexer_1_out12), .out13(demultiplexer_1_out13), .out14(demultiplexer_1_out14),
    .out15(demultiplexer_1_out15), .in(1'b1));  // open: sel, en
  Demultiplexer #(.select(2), .enable("false")) demultiplexer_2 (
    .out0(demultiplexer_2_out0), .out2(demultiplexer_2_out2), .out3(demultiplexer_2_out3), .in(COMMAND[16]),
    .sel(COMMAND[9:8]));  // open: out1
  DISPLAY_COL display_col_1 (
    .out_8(out_3), .out_9(display_col_1_out_9), .WRT_CLK(undriven_4), .ENABLE(demultiplexer_1_out0),
    .CLEAR(undriven_5), .COMMIT(undriven_6), .DATA(undriven), .ADDR(undriven_2), .VALUE(undriven_3));
  DISPLAY_COL display_col_2 (
    .out_8(out_4), .out_9(display_col_1_out_9), .WRT_CLK(undriven_4), .ENABLE(demultiplexer_1_out1),
    .CLEAR(undriven_5), .COMMIT(undriven_6), .DATA(undriven), .ADDR(undriven_2), .VALUE(undriven_3));
  DISPLAY_COL display_col_3 (
    .out_8(out_5), .out_9(display_col_1_out_9), .WRT_CLK(undriven_4), .ENABLE(demultiplexer_1_out2),
    .CLEAR(undriven_5), .COMMIT(undriven_6), .DATA(undriven), .ADDR(undriven_2), .VALUE(undriven_3));
  DISPLAY_COL display_col_4 (
    .out_8(out_6), .out_9(display_col_1_out_9), .WRT_CLK(undriven_4), .ENABLE(demultiplexer_1_out3),
    .CLEAR(undriven_5), .COMMIT(undriven_6), .DATA(undriven), .ADDR(undriven_2), .VALUE(undriven_3));
  DISPLAY_COL display_col_5 (
    .out_8(out_7), .out_9(display_col_1_out_9), .WRT_CLK(undriven_4), .ENABLE(demultiplexer_1_out4),
    .CLEAR(undriven_5), .COMMIT(undriven_6), .DATA(undriven), .ADDR(undriven_2), .VALUE(undriven_3));
  DISPLAY_COL display_col_6 (
    .out_8(out_8), .out_9(display_col_1_out_9), .WRT_CLK(undriven_4), .ENABLE(demultiplexer_1_out5),
    .CLEAR(undriven_5), .COMMIT(undriven_6), .DATA(undriven), .ADDR(undriven_2), .VALUE(undriven_3));
  DISPLAY_COL display_col_7 (
    .out_8(out_9), .out_9(display_col_1_out_9), .WRT_CLK(undriven_4), .ENABLE(demultiplexer_1_out6),
    .CLEAR(undriven_5), .COMMIT(undriven_6), .DATA(undriven), .ADDR(undriven_2), .VALUE(undriven_3));
  DISPLAY_COL display_col_8 (
    .out_8(out_10), .out_9(display_col_1_out_9), .WRT_CLK(undriven_4), .ENABLE(demultiplexer_1_out7),
    .CLEAR(undriven_5), .COMMIT(undriven_6), .DATA(undriven), .ADDR(undriven_2), .VALUE(undriven_3));
  DISPLAY_COL display_col_9 (
    .out_8(out_11), .out_9(display_col_1_out_9), .WRT_CLK(undriven_4), .ENABLE(demultiplexer_1_out8),
    .CLEAR(undriven_5), .COMMIT(undriven_6), .DATA(undriven), .ADDR(undriven_2), .VALUE(undriven_3));
  DISPLAY_COL display_col_10 (
    .out_8(out_12), .out_9(display_col_1_out_9), .WRT_CLK(undriven_4), .ENABLE(demultiplexer_1_out9),
    .CLEAR(undriven_5), .COMMIT(undriven_6), .DATA(undriven), .ADDR(undriven_2), .VALUE(undriven_3));
  DISPLAY_COL display_col_11 (
    .out_8(out_13), .out_9(display_col_1_out_9), .WRT_CLK(undriven_4), .ENABLE(demultiplexer_1_out10),
    .CLEAR(undriven_5), .COMMIT(undriven_6), .DATA(undriven), .ADDR(undriven_2), .VALUE(undriven_3));
  DISPLAY_COL display_col_12 (
    .out_8(out_14), .out_9(display_col_1_out_9), .WRT_CLK(undriven_4), .ENABLE(demultiplexer_1_out11),
    .CLEAR(undriven_5), .COMMIT(undriven_6), .DATA(undriven), .ADDR(undriven_2), .VALUE(undriven_3));
  DISPLAY_COL display_col_13 (
    .out_8(out_15), .out_9(display_col_1_out_9), .WRT_CLK(undriven_4), .ENABLE(demultiplexer_1_out12),
    .CLEAR(undriven_5), .COMMIT(undriven_6), .DATA(undriven), .ADDR(undriven_2), .VALUE(undriven_3));
  DISPLAY_COL display_col_14 (
    .out_8(out_16), .out_9(display_col_1_out_9), .WRT_CLK(undriven_4), .ENABLE(demultiplexer_1_out13),
    .CLEAR(undriven_5), .COMMIT(undriven_6), .DATA(undriven), .ADDR(undriven_2), .VALUE(undriven_3));
  DISPLAY_COL display_col_15 (
    .out_8(out_17), .out_9(display_col_1_out_9), .WRT_CLK(undriven_4), .ENABLE(demultiplexer_1_out14),
    .CLEAR(undriven_5), .COMMIT(undriven_6), .DATA(undriven), .ADDR(undriven_2), .VALUE(undriven_3));
  DISPLAY_COL display_col_16 (
    .out_8(out_18), .out_9(display_col_1_out_9), .WRT_CLK(undriven_4), .ENABLE(demultiplexer_1_out15),
    .CLEAR(undriven_5), .COMMIT(undriven_6), .DATA(undriven), .ADDR(undriven_2), .VALUE(undriven_3));
endmodule

module DISPLAY_COL (
  input  [15:0] DATA,
  input  WRT_CLK,
  input  ENABLE,
  input  CLEAR,
  input  COMMIT,
  input  [3:0] ADDR,
  input  VALUE,
  output [15:0] out_8,
  output [15:0] out_9
);

  wire [15:0] multiplexer_1_out, register_1_q, set_bit_1_out;

  Multiplexer #(.width(16), .enable("false")) multiplexer_1 (
    .in0(set_bit_1_out), .in1(DATA), .out(multiplexer_1_out));  // open: sel
  Register #(.width(16)) register_1 (.D(multiplexer_1_out), .en(ENABLE), .Q(register_1_q), .clk(WRT_CLK), .clr(CLEAR));
  Register #(.width(16)) register_2 (.D(register_1_q), .Q(out_8), .clk(COMMIT), .clr(CLEAR));  // open: en
  SET_BIT set_bit_1 (.BIT(ADDR), .VALUE(VALUE), .IN(register_1_q), .OUT(set_bit_1_out));
  assign out_9 = ENABLE ? register_1_q : 16'bz;  // Controlled_Buffer controlled_buffer_1
endmodule

module SET_BIT (
  input  [3:0] BIT,
  input  VALUE,
  input  [15:0] IN,
  output [15:0] OUT
);

  wire demultiplexer_1_out0, demultiplexer_1_out1, demultiplexer_1_out2, demultiplexer_1_out3,
       demultiplexer_1_out4, demultiplexer_1_out5, demultiplexer_1_out6, demultiplexer_1_out7,
       demultiplexer_1_out8, demultiplexer_1_out9, demultiplexer_1_out10, demultiplexer_1_out11,
       demultiplexer_1_out12, demultiplexer_1_out13, demultiplexer_1_out14;

  Demultiplexer #(.select(4), .disabled(0), .enable("false")) demultiplexer_1 (
    .out0(demultiplexer_1_out0), .out1(demultiplexer_1_out1), .out2(demultiplexer_1_out2),
    .out3(demultiplexer_1_out3), .out4(demultiplexer_1_out4), .out5(demultiplexer_1_out5),
    .out6(demultiplexer_1_out6), .out7(demultiplexer_1_out7), .out8(demultiplexer_1_out8),
    .out9(demultiplexer_1_out9), .out10(demultiplexer_1_out10), .out11(demultiplexer_1_out11),
    .out12(demultiplexer_1_out12), .out13(demultiplexer_1_out13), .out14(demultiplexer_1_out14),
    .out15(demultiplexer_1_out14), .in(1'b1), .sel(BIT));
  Multiplexer #(.enable("false")) multiplexer_1 (.in0(IN[0]), .in1(VALUE), .out(OUT[0]), .sel(demultiplexer_1_out0));
  Multiplexer #(.enable("false")) multiplexer_2 (.in0(IN[1]), .in1(VALUE), .out(OUT[1]), .sel(demultiplexer_1_out1));
  Multiplexer #(.enable("false")) multiplexer_3 (.in0(IN[2]), .in1(VALUE), .out(OUT[2]), .sel(demultiplexer_1_out2));
  Multiplexer #(.enable("false")) multiplexer_4 (.in0(IN[3]), .in1(VALUE), .out(OUT[3]), .sel(demultiplexer_1_out3));
  Multiplexer #(.enable("false")) multiplexer_5 (.in0(IN[4]), .in1(VALUE), .out(OUT[4]), .sel(demultiplexer_1_out4));
  Multiplexer #(.enable("false")) multiplexer_6 (.in0(IN[5]), .in1(VALUE), .out(OUT[5]), .sel(demultiplexer_1_out5));
  Multiplexer #(.enable("false")) multiplexer_7 (.in0(IN[6]), .in1(VALUE), .out(OUT[6]), .sel(demultiplexer_1_out6));
  Multiplexer #(.enable("false")) multiplexer_8 (.in0(IN[7]), .in1(VALUE), .out(OUT[7]), .sel(demultiplexer_1_out7));
  Multiplexer #(.enable("false")) multiplexer_9 (.in0(IN[8]), .in1(VALUE), .out(OUT[8]), .sel(demultiplexer_1_out8));
  Multiplexer #(.enable("false")) multiplexer_10 (.in0(IN[9]), .in1(VALUE), .out(OUT[9]), .sel(demultiplexer_1_out9));
  Multiplexer #(.enable("false")) multiplexer_11 (
    .in0(IN[10]), .in1(VALUE), .out(OUT[10]), .sel(demultiplexer_1_out10));
  Multiplexer #(.enable("false")) multiplexer_12 (
    .in0(IN[11]), .in1(VALUE), .out(OUT[11]), .sel(demultiplexer_1_out11));
  Multiplexer #(.enable("false")) multiplexer_13 (
    .in0(IN[12]), .in1(VALUE), .out(OUT[12]), .sel(demultiplexer_1_out12));
  Multiplexer #(.enable("false")) multiplexer_14 (
    .in0(IN[13]), .in1(VALUE), .out(OUT[13]), .sel(demultiplexer_1_out13));
  Multiplexer #(.enable("false")) multiplexer_15 (
    .in0(IN[14]), .in1(VALUE), .out(OUT[14]), .sel(demultiplexer_1_out14));
  Multiplexer #(.enable("false")) multiplexer_16 (
    .in0(IN[15]), .in1(VALUE), .out(OUT[15]), .sel(demultiplexer_1_out14));
endmodule

module IS_NOT_ZERO (
  input  [15:0] in_1,
  output [15:0] out_2
);

  or or_1 (out_2[15], in_1[0], in_1[1], in_1[2], in_1[3], in_1[4], in_1[5], in_1[6], in_1[7], in_1[9], in_1[10], in_1[11], in_1[12], in_1[13], in_1[14], in_1[15], in_1[8]);

  assign out_2[14:0] = {15{out_2[15]}};
endmodule
